// Logisim project control_logic.circ as structural Verilog: 1 circuit, main circuit control_logic
module control_logic (
  input  [31:0] inst,
  input  BrEq,
  input  BrLt,
  output PCSel,
  output RegWEn,
  output [2:0] ImmSel,
  output BrUn,
  output ASel,
  output BSel,
  output [3:0] ALUSel,
  output MemRW,
  output [1:0] WBSel,
  output CSRSel,
  output CSRWen
);

  wire comparator_1_eq, comparator_2_eq, comparator_3_eq, comparator_4_eq, comparator_7_eq, comparator_8_eq,
       IType, not_1_out, or_3_out, RType, SBType, SType, UJType, UType;

  Comparator #(.width(7)) comparator_1 (.a(inst[6:0]), .b(7'b0000011), .eq(comparator_1_eq));  // open: gt, lt
  Comparator #(.width(7)) comparator_2 (.a(inst[6:0]), .b(7'b0010011), .eq(comparator_2_eq));  // open: gt, lt
  Comparator #(.width(7)) comparator_3 (.a(inst[6:0]), .b(7'b1100111), .eq(comparator_3_eq));  // open: gt, lt
  Comparator #(.width(7)) comparator_4 (.a(inst[6:0]), .b(7'b1110011), .eq(comparator_4_eq));  // open: gt, lt
  Comparator #(.width(7)) comparator_5 (.a(inst[6:0]), .b(7'b0100011), .eq(SType));  // open: gt, lt
  Comparator #(.width(7)) comparator_6 (.a(inst[6:0]), .b(7'b1100011), .eq(SBType));  // open: gt, lt
  Comparator #(.width(7)) comparator_7 (.a(inst[6:0]), .b(7'b0010111), .eq(comparator_7_eq));  // open: gt, lt
  Comparator #(.width(7)) comparator_8 (.a(inst[6:0]), .b(7'b0110111), .eq(comparator_8_eq));  // open: gt, lt
  Comparator #(.width(7)) comparator_9 (.a(inst[6:0]), .b(7'b1101111), .eq(UJType));  // open: gt, lt
  Comparator #(.width(7)) comparator_10 (.a(inst[6:0]), .b(7'b0110011), .eq(RType));  // open: gt, lt
  or or_1 (IType, comparator_1_eq, comparator_2_eq, comparator_3_eq, comparator_4_eq);
  or or_2 (UType, comparator_7_eq, comparator_8_eq);
  assign ImmSel = IType ? 3'b000 : 3'bz;  // Controlled_Buffer controlled_buffer_1
  assign ImmSel = SType ? 3'b001 : 3'bz;  // Controlled_Buffer controlled_buffer_2
  assign ImmSel = SBType ? 3'b010 : 3'bz;  // Controlled_Buffer controlled_buffer_3
  assign ImmSel = UType ? 3'b011 : 3'bz;  // Controlled_Buffer controlled_buffer_4
  assign ImmSel = UJType ? 3'b100 : 3'bz;  // Controlled_Buffer controlled_buffer_5
  assign ASel = IType ? 1'b0 : 1'bz;  // Controlled_Buffer controlled_buffer_6
  assign BSel = IType ? 1'b1 : 1'bz;  // Controlled_Buffer controlled_buffer_7
  or or_3 (or_3_out, SBType, UJType);
  assign PCSel = or_3_out ? 1'b1 : 1'bz;  // Controlled_Buffer controlled_buffer_8
  not not_1 (not_1_out, or_3_out);
  assign PCSel = not_1_out ? 1'b0 : 1'bz;  // Controlled_Buffer controlled_buffer_9
  assign WBSel = IType ? 2'b01 : 2'bz;  // Controlled_Buffer controlled_buffer_10
  assign RegWEn = IType ? 1'b1 : 1'bz;  // Controlled_Buffer controlled_buffer_11

  assign ALUSel = 4'b0000;

  // Other names for the same wires on the sheet: opcode[6:0] = inst[6:0]; rd[4:0] = inst[11:7];
  //   funct3[2:0] = inst[14:12]; rs1[4:0] = inst[19:15]; rs2[4:0] = inst[24:20]; funct7[6:0] = inst[31:25]

  // Notes on the sheet:
  //   INPUTS to your circuit
  //   DON'T CHANGE THE LOCATIONS OF THE INPUTS AND OUTPUTS!
  //   OUTPUT from your circuit
endmodule
