// Logisim project imm_gen.circ as structural Verilog: 1 circuit, main circuit imm_gen
module imm_gen (
  input  [31:0] inst,
  input  [2:0] ImmSel,
  output [31:0] imm
);

  wire [31:0] IType, SBType, SType, UJType, UType;

  // Probe on inst[31:20]
  // Probe on IType
  assign IType = {{20{inst[31]}}, inst[31:20]};  // Bit_Extender bit_extender_1
  Multiplexer #(.enable("false"), .select(3), .width(32)) multiplexer_1 (
    .in0(IType), .in1(SType), .in2(SBType), .in3(UType), .in4(UJType), .out(imm), .sel(ImmSel));  // open: in5, in6, in7

  // Other names for the same wires on the sheet: rs2[4:0] = inst[24:20]; funct7[6:0] = inst[31:25];
  //   opcode[6:0] = inst[6:0]; rd[4:0] = inst[11:7]; funct3[2:0] = inst[14:12]; rs1[4:0] = inst[19:15]

  // Notes on the sheet:
  //   INPUTS to your circuit
  //   DON'T CHANGE THE LOCATIONS OF THE INPUTS AND OUTPUTS!
  //   0:I, 1:S, 2:SB, 3:U, 4:UJ
  //   OUTPUT from your circuit
endmodule
